# Fritzing sketch trinket 12v controller (saved by Fritzing 0.9.3b)
circuit board: 4.25836cm x 4.64619cm
breadboards: 1

parts:
  Q1 = MOSFET-NCHANNEL [package=to220v]
  Q2 = MOSFET-NCHANNEL [package=to220v]
  R2 = Resistor [tolerance=±5% resistance=220 package=THT]
  R1 = Resistor [tolerance=±5% resistance=220 package=THT]
  Part1 = Adafruit Trinket 5V
  U2 = Voltage Regulator - 5V [package="TO220 [THT]"]
  JP1 = Header 2 [package=jst-2-pth-ns]
  JP2 = Header 2 [package=jst-2-pth-ns]
  JP3 = Header 2 [package=jst-2-pth-ns]
  S2 = Pushbutton [package="[THT]"]

nets:
  N1: Q1.G, R1.Pin_0, Part1.#0
  N2: Q1.D, JP2.1
  GND: Q1.S, Q2.S, R2.Pin_1, R1.Pin_1, Part1.GND, U2.GND, JP3.1
  N3: Q2.G, R2.Pin_0, Part1.#1
  N4: Q2.D, JP1.1
  N5: Part1.VBAT, U2.input_voltage, JP1.2, JP2.2, JP3.2
  N6: Part1.#4, S2.Pin_3, S2.Pin_4
  N7: U2.output_voltage, S2.Pin_1, S2.Pin_2

notes:
  12v LED Switcher
  V1.0 6/3/2017

custom parts:
  Adafruit Trinket 5V: Trinket may be small, but do not be fooled by its size! It's a tiny microcontroller board, built around the Atmel ATtiny85, a little chip with a lot of power. We wanted to design a microcontroller board that was small enough to fit into any project, and low cost enough to use without hesitation. Perfect for when you don't want to give up your expensive dev-board and you aren't willing to take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
